# Fritzing sketch Sketch (saved by Fritzing 0.9.3b)
circuit board: 6.23523cm x 6.67516cm
breadboards: 1

parts:
  ESP32 = ESP-WROOM-32 [ESP-32S] Module [part_number=ESP-WROOM-32]
  LCD1 = TFT 1.8 inch 160x128 w SD
  S1 = Momentary Switch [package=ksa_sealed_tac_switch]
  S2 = Momentary Switch [package=ksa_sealed_tac_switch]
  S3 = Momentary Switch [package=ksa_sealed_tac_switch]
  S4 = Momentary Switch [package=ksa_sealed_tac_switch]

nets:
  N1: ESP32.GND, LCD1.pin2
  N2: ESP32.3V3, LCD1.pin_1, LCD1.pin_8, S1.2, S2.2, S3.2, S4.2
  N3: ESP32.IO15, S1.3
  N4: ESP32.IO2, LCD1.pin_5
  N5: ESP32.IO0, S2.3
  N6: ESP32.IO4, LCD1.pin4
  N7: ESP32.IO16, S3.3
  N8: ESP32.IO17, S4.3
  N9: ESP32.IO5, LCD1.pin3
  N10: ESP32.IO18, LCD1.pin_7
  N11: ESP32.IO23, LCD1.pin_6

custom parts:
  ESP-WROOM-32 [ESP-32S] Module: Espressif ESP-WROOM-32 WiFi/Bluetooth LE microcontroller module also known as the Ai-Thinker ESP-32S module with similar formfactor. The ESP32 is a microcontroller chip with WiFi and BLE capabilities. The chip is developed by Espressif and is the successor to the popular ESP8266 WiFi module.
  TFT 1.8 inch 160x128 w SD: This is a generic 1.8 tft spi lcd display available on ebay and others. The 1.8" display has 128x160 color pixels.
